// Logisim project Lab7.circ as structural Verilog: 3 circuits, main circuit ParityGenerator
module XOR (
  input  X,
  input  Y,
  input  X_2,
  input  Y_2,
  output out_5,
  output out_6
);

  wire and_1_out, and_3_out, and_4_out, not_1_out, not_2_out, not_3_out, or_1_out;

  not not_1 (not_1_out, X_2);
  not not_2 (not_2_out, and_1_out);
  and and_1 (and_1_out, Y, X);
  or or_1 (or_1_out, Y, X);
  not not_3 (not_3_out, Y_2);
  and and_2 (out_5, not_2_out, or_1_out);
  and and_3 (and_3_out, not_3_out, X_2);
  and and_4 (and_4_out, Y_2, not_1_out);
  or or_2 (out_6, and_3_out, and_4_out);

  // Notes on the sheet:
  //   x XOR y = (x or y) and not (x and y)
  //   Minterm Expansion
  //   Both circuits are equivalent and valid representations of x XOR y
endmodule

module MyXOR (
);


  // Notes on the sheet:
  //   Practice using Logism by recreating one of the implementations from XOR!
endmodule

module ParityGenerator (
  input  X,
  input  Y,
  input  Z,
  output Parity
);

  wire and_1_out, and_2_out, and_3_out, and_4_out, and_5_out, and_6_out, and_7_out, and_8_out, and_9_out,
       not_1_out, not_2_out, not_3_out, not_4_out, not_5_out, not_6_out, not_7_out, not_8_out, or_1_out,
       or_2_out, or_3_out;

  not not_1 (not_1_out, Z);
  and and_1 (and_1_out, X, Y);
  and and_2 (and_2_out, and_1_out, not_1_out);
  and and_3 (and_3_out, Y, Z);
  not not_2 (not_2_out, X);
  and and_4 (and_4_out, not_2_out, and_3_out);
  or or_1 (or_1_out, and_2_out, or_2_out);
  not not_3 (not_3_out, X);
  and and_5 (and_5_out, not_3_out, and_6_out);
  or or_2 (or_2_out, and_4_out, and_5_out);
  and and_6 (and_6_out, Y, Z);
  or or_3 (or_3_out, not_6_out, and_8_out);
  not not_4 (not_4_out, X);
  not not_5 (not_5_out, Y);
  and and_7 (and_7_out, not_4_out, not_5_out);
  and and_8 (and_8_out, and_7_out, not_8_out);
  not not_6 (not_6_out, or_1_out);
  and and_9 (and_9_out, not_6_out, and_8_out);
  not not_7 (not_7_out, and_9_out);
  and and_10 (Parity, or_3_out, not_7_out);
  not not_8 (not_8_out, Z);

  // Notes on the sheet:
  //   Input Bits
  //   Output Bit
  //   If there are only 2 inputs this fires -->
  //   Write your parity circuit here
  //   the output = 1 if an odd number of inputs (1 or 3) are 1, otherwise 0
  //   ONLY use: NOT, AND, OR, and any custom functions you write (included in the .circ submission)
  //   WRITE YOUR NAME AND PLEDGE SOMEWHERE IN THIS CIRCUIT
  //   <-- If there are no inputs this fires
  //   <-- This is an xor gate made from and/or/not gates
  //   Name: Maxwell Metzner
  //   I pledge my honor that I have abided by the Stevens Honor System
endmodule
